// Logisim project crapph.circ as structural Verilog: 1 circuit, main circuit main
module main (
);

  wire clock_1_out, decoder_1_out0, decoder_1_out1, decoder_1_out2, decoder_1_out3, decoder_1_out4,
       decoder_1_out5, decoder_1_out6, decoder_1_out7, decoder_1_out14, decoder_1_out15, not_1_out,
       not_2_out, or_1_out, or_2_out, or_3_out, t_ff_1_q;
  wire [7:0] adder_1_out, controlled_buffer_1_out, counter_1_q, register_1_q, register_2_q, register_3_q;
  wire [11:0] rom_1_data;

  T_Flip_Flop t_ff_1 (.clk(clock_1_out), .T(decoder_1_out14), .Q(t_ff_1_q));  // open: Qn, preset, reset
  not not_1 (not_1_out, t_ff_1_q);
  Clock clock_1 (.out(clock_1_out));
  ROM #(.dataWidth(12)) rom_1 (.addr(counter_1_q), .data(rom_1_data));
  Counter counter_1 (
    .load(decoder_1_out15), .D(controlled_buffer_1_out), .Q(counter_1_q), .up(not_1_out), .clk(clock_1_out));  // open: count, carry, clr
  Decoder #(.select(4)) decoder_1 (
    .out0(decoder_1_out0), .out1(decoder_1_out1), .out2(decoder_1_out2), .out3(decoder_1_out3),
    .out4(decoder_1_out4), .out5(decoder_1_out5), .out6(decoder_1_out6), .out7(decoder_1_out7),
    .out14(decoder_1_out14), .out15(decoder_1_out15), .sel(rom_1_data[11:8]));  // open: out8, out9, out10, out11, out12, out13, en
  assign controlled_buffer_1_out = not_2_out ? rom_1_data[7:0] : 8'bz;  // Controlled_Buffer controlled_buffer_1
  not not_2 (not_2_out, or_1_out);
  or or_1 (or_1_out, decoder_1_out6, decoder_1_out5, decoder_1_out7);
  assign controlled_buffer_1_out = decoder_1_out3 ? register_2_q : 8'bz;  // Controlled_Buffer controlled_buffer_2
  assign controlled_buffer_1_out = decoder_1_out1 ? register_1_q : 8'bz;  // Controlled_Buffer controlled_buffer_3
  or or_2 (or_2_out, decoder_1_out6, decoder_1_out7);
  assign controlled_buffer_1_out = or_2_out ? adder_1_out : 8'bz;  // Controlled_Buffer controlled_buffer_4
  assign controlled_buffer_1_out = decoder_1_out5 ? register_3_q : 8'bz;  // Controlled_Buffer controlled_buffer_5
  Register register_1 (
    .D(controlled_buffer_1_out), .en(decoder_1_out0), .clk(clock_1_out), .Q(register_1_q));  // open: clr
  Register register_2 (
    .D(controlled_buffer_1_out), .en(decoder_1_out2), .clk(clock_1_out), .Q(register_2_q));  // open: clr
  Adder adder_1 (.a(register_2_q), .b(register_1_q), .out(adder_1_out));  // open: cin, cout
  Register register_3 (.D(controlled_buffer_1_out), .en(or_3_out), .clk(clock_1_out), .Q(register_3_q));  // open: clr
  or or_3 (or_3_out, decoder_1_out4, decoder_1_out7);

  // Notes on the sheet:
  //   contents of rom_1 (hex, n*v repeats v):
  //   53 0 201 521 700
endmodule
